# Fritzing sketch try_attiny85_watchdog_and_user_interrupt (saved by Fritzing 0.9.9b)
breadboards: 2

parts:
  IC1 = IC, DIP package, 8 pins [chip_label=ATtiny]
  LED1 = LED - 5mm [color="Green (555nm)" current=0.030 package="5 mm [THT]"]
  R2 = Resistor [tolerance=±5% power=0.25 resistance=220 package=THT]
  S1 = Pushbutton [package="[THT]"]
  Part1 = DC Voltage Source 5V [package=THT]
  S2 = Pushbutton [package="[THT]"]
  R3 = Resistor [tolerance=±5% power=0.25 resistance=220 package=THT]
  LED2 = LED - 5mm [color="Yellow (595nm)" current=0.030 package="5 mm [THT]"]
  Part2 = Arduino Uno (Rev3) - ICSP

nets:
  N1: IC1.pin2, S2.Pin_3, S2.Pin_4, Part2.D8
  N2: IC1.pin4, R2.Pin_0, S1.Pin_3, S1.Pin_4, Part1.V–, S2.Pin_1, S2.Pin_2, R3.Pin_0
  N3: IC1.pin5, LED1.cathode, Part2.D13/SCK
  N4: IC1.pin6, LED2.anode, Part2.D12/MISO
  N5: IC1.pin7, S1.Pin_1, S1.Pin_2, Part2.D2
  N6: IC1.pin8, Part1.V+
  N7: LED1.anode, R3.Pin_1
  N8: R2.Pin_1, LED2.cathode

notes:
  INT0
  PCINT0
  Watchdog time-out
  Sleep-interrupt
  WIRE EITHER
  - Arduino UNO
  - ATtiny
  BUT NOT BOTH AT THE SAME TIME

custom parts:
  DC Voltage Source 5V: A dummy, proxy, ersatz, stand-in part for whatever you want. With 3 pins on a 100 mil inline pin header footprint.
